# Fritzing sketch Schematic (saved by Fritzing 0.9.3b)
breadboards: 1

parts:
  Part1 = Arduino Uno (Rev3)
  LED1 = RGB LED (com. cathode, rbg) [package="5 mm [THT]"]
  R1 = Resistor [tolerance=±5% resistance=220 package=THT]
  R2 = Resistor [tolerance=±5% resistance=220 package=THT]
  R3 = Resistor [tolerance=±5% resistance=220 package=THT]
  Q1 = LTR-301 [package=ltr-301]
  Q2 = LTR-301 [package=ltr-301]
  R4 = Resistor [tolerance=±5% resistance=10k package=THT]
  R5 = Resistor [tolerance=±5% resistance=10k package=THT]
  R6 = Resistor [tolerance=±5% resistance=10k package=THT]
  Q3 = LTR-301 [package=ltr-301]

nets:
  N1: Part1.A0, R4.Pin_0, Q3.E
  N2: Part1.A1, Q1.E, R5.Pin_0
  N3: Part1.A2, Q2.E, R6.Pin_0
  N4: Part1.D9_PWM, R3.Pin_1
  N5: Part1.D10_PWM/SS, R1.Pin_1
  N6: Part1.D11_PWM/MOSI, R2.Pin_1
  N7: Part1.5V, Q1.C, Q2.C, Q3.C
  N8: Part1.GND, LED1.common_cathode, R4.Pin_1, R5.Pin_1, R6.Pin_1
  N9: LED1.red_anode, R1.Pin_0
  N10: LED1.blue_anode, R2.Pin_0
  N11: LED1.green_anode, R3.Pin_0
