# Fritzing sketch Schematic (saved by Fritzing 0.9.3b)
breadboards: 1

parts:
  Part1 = Arduino Uno (Rev3)
  U1 = LCD-16X2 [package=lcd-16x2]
  R1 = TRIMPOT [package=3386u]
  S1 = Tilt Switch [package=THT]
  R2 = Resistor [tolerance=±5% resistance=220 package=THT]
  R3 = Resistor [tolerance=±5% resistance=10k package=THT]

nets:
  N1: Part1.D11_PWM/MOSI, U1.DB4
  N2: Part1.D12/MISO, U1.DB6
  GND: Part1.GND, U1.VSS, U1.DB5, U1.K, R1.CW, R3.Pin_0
  N3: Part1.D2, U1.VO
  N4: Part1.D3_PWM, U1.RS
  N5: Part1.D4, U1.R_W
  N6: Part1.D5_PWM, U1.E
  N7: Part1.D6_PWM, S1.Pin_2, R3.Pin_1
  N8: Part1.5V, U1.A, R1.CCW, S1.Pin_1, R2.Pin_0
  N9: U1.VDD, R2.Pin_1
  N10: U1.DB7, R1.WIPER
