# Fritzing sketch Schematic (saved by Fritzing 0.9.3b)
breadboards: 1

parts:
  Part1 = Arduino Uno (Rev3)
  R1 = Resistor [tolerance=±5% resistance=220 package=THT]
  R3 = Resistor [tolerance=±5% resistance=220 package=THT]
  R2 = Resistor [tolerance=±5% resistance=220 package=THT]
  R4 = Resistor [tolerance=±5% resistance=10k package=THT]
  R5 = Resistor [tolerance=±5% resistance=1M package=THT]
  LED1 = LED - 5mm [color="Red (633nm)" package="5 mm [THT]"]
  LED2 = LED - 5mm [color="Yellow (592nm)" package="5 mm [THT]"]
  LED3 = LED - 5mm [color="Green (570nm)" package="5 mm [THT]"]
  S1 = Pushbutton [package="[THT]"]
  J2 = Basic Servo
  C1 = Electrolytic Capacitor [capacitance=0.1mF package="100 mil [THT, electrolytic]"]
  J1 = Piezo Speaker

nets:
  N1: Part1.A0, R5.Pin_0, J1.pin1
  N2: Part1.D9_PWM, J2.pulse
  GND: Part1.GND, R4.Pin_0, R5.Pin_1, LED1.cathode, LED2.cathode, LED3.cathode, J2.gnd, C1.-
  N3: Part1.D2, R4.Pin_1, S1.Pin_4
  N4: Part1.D3_PWM, R1.Pin_0
  N5: Part1.D4, R2.Pin_0
  N6: Part1.D5_PWM, R3.Pin_0
  5V: Part1.5V, S1.Pin_1, S1.Pin_2, J2.vcc, J1.pin2
  N7: R1.Pin_1, LED2.anode
  N8: R3.Pin_1, LED1.anode
  N9: R2.Pin_1, LED3.anode
