# Fritzing sketch Schematic (saved by Fritzing 0.9.3b)
breadboards: 1

parts:
  Part1 = Arduino Uno (Rev3)
  LS1 = Piezo Speaker
  R1 = Resistor [tolerance=±5% resistance=10k package=THT]
  Q1 = LTR-301 [package=ltr-301]
  R2 = Resistor [tolerance=±5% resistance=10k package=THT]

nets:
  N1: Part1.A0, R1.Pin_0, Q1.E
  N2: Part1.D8, R2.Pin_0
  N3: Part1.GND, LS1.pin2, R1.Pin_1
  N4: Part1.5V, Q1.C
  N5: LS1.pin1, R2.Pin_1
