# Fritzing sketch Schematic (saved by Fritzing 0.9.3b)
breadboards: 1

parts:
  T2 = TMP36 Temperature Sensor [package="TO92 [THT]"]
  Part1 = Arduino Uno (Rev3)
  LED1 = LED - 5mm [color="Red (633nm)" package="5 mm [THT]"]
  LED2 = LED - 5mm [color="Orange (620nm)" package="5 mm [THT]"]
  LED3 = LED - 5mm [color="Orange (620nm)" package="5 mm [THT]"]
  LED4 = LED - 5mm [color="Orange (620nm)" package="5 mm [THT]"]
  LED5 = LED - 5mm [color="Green (555nm)" package="5 mm [THT]"]
  R1 = Resistor [tolerance=±5% resistance=220 package=THT]
  R2 = Resistor [tolerance=±5% resistance=220 package=THT]  # not connected
  R3 = Resistor [tolerance=±5% resistance=220 package=THT]
  R4 = Resistor [tolerance=±5% resistance=220 package=THT]
  R5 = Resistor [tolerance=±5% resistance=220 package=THT]

nets:
  N1: T2.+Vs, Part1.5V
  N2: T2.Vout, Part1.A0
  N3: T2.GND, R1.Pin_0, R3.Pin_0, R4.Pin_0, R5.Pin_0
  N4: Part1.D2, LED5.anode
  N5: Part1.D3_PWM, LED4.anode
  N6: Part1.D4, LED3.anode
  N7: Part1.D5_PWM, LED2.anode
  N8: Part1.D6_PWM, LED1.anode
