# Fritzing sketch Schematic (saved by Fritzing 0.9.3b)
breadboards: 1

parts:
  Part1 = Arduino Uno (Rev3)
  J1 = Basic Servo
  C1 = Electrolytic Capacitor [capacitance=100µF package="200 mil [THT, electrolytic]"]
  R1 = TRIMPOT [package=trimpot_pth_s3_lock]
  C2 = Electrolytic Capacitor [capacitance=100µF package="200 mil [THT, electrolytic]"]

nets:
  N1: Part1.A0, R1.WIPER
  N2: Part1.D9_PWM, J1.pulse
  N3: Part1.GND, C2.-
  5V: Part1.5V, J1.vcc, C1.+, R1.CCW, C2.+
  N4: J1.gnd, C1.-
