# Fritzing sketch Schematic (saved by Fritzing 0.9.3b)
breadboards: 1

parts:
  Part1 = Arduino Uno (Rev3)
  R1 = Resistor [tolerance=±5% resistance=10k package=THT]
  M1 = DC Motor
  D1 = Rectifier Diode [part_number=1N4007 package="300 mil [THT]"]
  VCC1 = Battery block 9V
  S1 = Pushbutton [package="[THT]"]
  Q1 = Basic FET P-Channel [package="TO220 [THT]"]

nets:
  N1: Part1.D9_PWM, Q1.gate
  N2: Part1.GND, R1.Pin_1, VCC1.-, Q1.source
  N3: Part1.D2, R1.Pin_0, S1.Pin_3, S1.Pin_4
  N4: Part1.5V, S1.Pin_1, S1.Pin_2
  N5: M1.pin_1, D1.cathode, VCC1.+
  N6: M1.pin_2, D1.anode, Q1.drain
