# Fritzing sketch Schematic (saved by Fritzing 0.9.3b)
breadboards: 1

parts:
  Part1 = Arduino Uno (Rev3)
  Part2 = Arduino Uno (Rev3)
  U1 = LCD-16X2 [package=lcd-8x2]
  R1 = Resistor [tolerance=±5% resistance=220 package=THT]
  R2 = TRIMPOT [package=trimpot_tc33]
  KEYPAD1 = Membrane Matrix Keypad
  LED1 = smd LED [color="Red (633nm)" package="1206 [SMD]"]
  LED2 = smd LED [color="Green (560nm)" package="1206 [SMD]"]
  LED3 = smd LED [color="Yellow (595nm)" package="1206 [SMD]"]
  R3 = Resistor [tolerance=±5% resistance=220 package=THT]
  R4 = Resistor [tolerance=±5% resistance=220 package=THT]
  R5 = Resistor [tolerance=±5% resistance=220 package=THT]
  J1 = Basic Servo

nets:
  N1: Part1.A5/SCL, Part2.A5/SCL
  N2: Part1.D11_PWM/MOSI, U1.DB4
  N3: Part1.D12/MISO, U1.DB6
  GND: Part1.GND, Part2.GND, U1.VSS, U1.DB5, U1.K, R2.CW, LED1.cathode, LED2.cathode, LED3.cathode, J1.gnd
  N4: Part1.A4/SDA, Part2.A4/SDA
  N5: Part1.D2, U1.VO
  N6: Part1.D3_PWM, U1.RS
  N7: Part1.D4, U1.R_W
  N8: Part1.D5_PWM, U1.E
  N9: Part1.5V, U1.A, R1.Pin_0, R2.CCW
  N10: Part2.D8, KEYPAD1.5
  N11: Part2.D9_PWM, KEYPAD1.4
  N12: Part2.D10_PWM/SS, KEYPAD1.3
  N13: Part2.D11_PWM/MOSI, KEYPAD1.2
  N14: Part2.D12/MISO, KEYPAD1.1
  N15: Part2.D2, R3.Pin_1
  N16: Part2.D3_PWM, R4.Pin_1
  N17: Part2.D4, R5.Pin_1
  N18: Part2.D5_PWM, J1.pulse
  N19: Part2.D6_PWM, KEYPAD1.7
  N20: Part2.D7, KEYPAD1.6
  5V: Part2.5V, J1.vcc
  N21: U1.VDD, R1.Pin_1
  N22: U1.DB7, R2.WIPER
  N23: LED1.anode, R3.Pin_0
  N24: LED2.anode, R5.Pin_0
  N25: LED3.anode, R4.Pin_0

custom parts:
  Membrane Matrix Keypad: Membrane Matrix 3x4 Keypad
