# Fritzing sketch Schematic (saved by Fritzing 0.9.3b)
breadboards: 1

parts:
  Part1 = Arduino Uno (Rev3)
  LED1 = smd LED [color="Green (560nm)" package="0603 [SMD]"]
  LED2 = smd LED [color="Red (633nm)" package="0603 [SMD]"]
  LED3 = smd LED [color="Red (633nm)" package="0603 [SMD]"]
  R1 = Resistor [tolerance=±5% resistance=220 package=THT]
  R2 = Resistor [tolerance=±5% resistance=220 package=THT]
  R3 = Resistor [tolerance=±5% resistance=220 package=THT]
  S1 = Pushbutton [package="[THT]"]
  R5 = Resistor [tolerance=±5% resistance=10k package=THT]

nets:
  N1: Part1.GND, R1.Pin_0, R2.Pin_0, R3.Pin_0, R5.Pin_0
  N2: Part1.D2, S1.Pin_3, S1.Pin_4, R5.Pin_1
  N3: Part1.D3_PWM, LED1.anode
  N4: Part1.D4, LED2.anode
  N5: Part1.D5_PWM, LED3.anode
  N6: Part1.5V, S1.Pin_1, S1.Pin_2
  N7: LED1.cathode, R1.Pin_1
  N8: LED2.cathode, R2.Pin_1
  N9: LED3.cathode, R3.Pin_1
