# Fritzing sketch Schematic (saved by Fritzing 0.9.3b)
breadboards: 1

parts:
  R1 = Resistor [tolerance=±5% resistance=10k package=THT]
  R2 = Resistor [tolerance=±5% resistance=10k package=THT]
  VCC1 = Battery block 9V
  IC1 = L293D [package=THT]
  R3 = TRIMPOT [package=3386u]
  Part1 = Arduino Uno (Rev3)
  S1 = Pushbutton [package="[THT]"]
  S2 = Pushbutton [package="[THT]"]
  M1 = DC Motor

nets:
  N1: R1.Pin_0, R2.Pin_0, VCC1.-, IC1.0V, R3.CW, Part1.GND
  N2: R1.Pin_1, Part1.D4, S1.Pin_3, S1.Pin_4
  N3: R2.Pin_1, Part1.D5_PWM, S2.Pin_3, S2.Pin_4
  N4: VCC1.+, IC1.+Vmotor
  N5: IC1.Enable_1, Part1.D9_PWM
  N6: IC1.In_1, Part1.D3_PWM
  N7: IC1.Out_1_(_Controlled_by_Enable_1_), M1.pin_2
  N8: IC1.Out_2_(_Controlled_by_Enable_1_), M1.pin_1
  N9: IC1.In_2, Part1.D2
  N10: IC1.+V, R3.CCW, Part1.5V, S1.Pin_1, S1.Pin_2, S2.Pin_1, S2.Pin_2
  N11: R3.WIPER, Part1.A0
